# Fritzing sketch Fan (saved by Fritzing 0.9.3b)

parts:
  U10 = SWITCH_SPDT [package=kps-1290]
  C3 = Ceramic Capacitor [capacitance="100 nF" package="0603 [SMD, multilayer]"]
  C4 = Ceramic Capacitor [capacitance="100 nF" package="0603 [SMD, multilayer]"]
  VCC3 = Battery block 9V
  U11 = ESP8266 WiFi Module [part_number=ESP8266]
  U12 = Voltage Regulator - 5V [package="TO220 [THT]"]
  S6 = Pushbutton [package="[SMD]"]
  U13 = Voltage Regulator - 3.3V [package="TO220 [THT]"]
  IR4 = TSOP312.., 314.. [package=THT]
  S7 = H-Bridge with L298N
  M4 = DC Motor

nets:
  N1: U10.P, U12.input_voltage, U13.input_voltage
  GND: U10.S, C3.0, C4.1, VCC3.-, U11.GND, U12.GND, S6.Pin_3, S6.Pin_4, U13.GND, IR4.GND, S7.GND, S7.IN2
  N2: C3.1, U11.VCC, U13.output_voltage
  N3: C4.0, U12.output_voltage, IR4.Vs, S7.12V, S7.IN1
  N4: U11.GPIO_0, S7.ENA
  N5: U11.RST, S6.Pin_1, S6.Pin_2
  N6: U11.GPIO_2, IR4.Data
  N7: S7.M1-01, M4.pin_2
  N8: S7.M1-02, M4.pin_1

custom parts:
  ESP8266 WiFi Module: Generic WiFi Module based on the ESP8266 with onboard PCB antenna and UART communications
  H-Bridge with L298N: h-bridge
