# Fritzing sketch IR Decoder (saved by Fritzing 0.9.3b)

parts:
  D1 = LTE-302 [package=lte-302]
  Part1 = Arduino Uno (Rev3) - ICSP
  R1 = Resistor [tolerance=±5% resistance=1k package="1206 [SMD]"]

nets:
  N1: D1.A, R1.Pin_1
  N2: D1.C, Part1.GND
  N3: Part1.A0, R1.Pin_0
