# Fritzing sketch Lamp (saved by Fritzing 0.9.3b)

parts:
  U4 = ESP8266 WiFi Module [part_number=ESP8266]
  U5 = Voltage Regulator - 5V [package="TO220 [THT]"]
  S3 = Pushbutton [package="[SMD]"]
  U6 = Voltage Regulator - 3.3V [package="TO220 [THT]"]
  LED2 = LED - 5mm [color="Red (633nm)" package="5 mm [THT]"]
  IR2 = TSOP312.., 314.. [package=THT]
  R1 = Resistor [tolerance=±5% resistance=1k package="2512 [SMD]"]
  U7 = SWITCH_SPDT [package=kps-1290]
  C1 = Ceramic Capacitor [capacitance="100 nF" package="0603 [SMD, multilayer]"]
  C2 = Ceramic Capacitor [capacitance="100 nF" package="0603 [SMD, multilayer]"]
  VCC1 = Battery block 9V

nets:
  N1: U4.VCC, U6.output_voltage, C2.1
  N2: U4.GPIO_0, R1.Pin_0
  N3: U4.RST, S3.Pin_1, S3.Pin_2
  N4: U4.GPIO_2, IR2.Data
  GND: U4.GND, U5.GND, S3.Pin_3, S3.Pin_4, U6.GND, LED2.anode, IR2.GND, U7.S, C1.1, C2.0, VCC1.-
  N5: U5.input_voltage, U6.input_voltage, U7.P
  N6: U5.output_voltage, IR2.Vs, C1.0
  N7: LED2.cathode, R1.Pin_1

custom parts:
  ESP8266 WiFi Module: Generic WiFi Module based on the ESP8266 with onboard PCB antenna and UART communications
