# Fritzing sketch MQ9-DHT (saved by Fritzing 0.9.3b)

parts:
  U13 = SWITCH_SPDT [package=kps-1290]
  C3 = Ceramic Capacitor [capacitance="100 nF" package="0603 [SMD, multilayer]"]
  C4 = Ceramic Capacitor [capacitance="100 nF" package="0603 [SMD, multilayer]"]
  VCC4 = Battery block 9V
  U14 = ESP8266 WiFi Module [part_number=ESP8266]
  U15 = Voltage Regulator - 5V [package="TO220 [THT]"]
  S6 = Pushbutton [package="[SMD]"]
  U16 = Voltage Regulator - 3.3V [package="TO220 [THT]"]
  DHT3 = DHT11 Humitidy and Temperature Sensor
  R2 = Resistor [tolerance=±5% resistance=1k package="2512 [SMD]"]
  Part5 = MQ-9 breakout

nets:
  N1: U13.P, U15.input_voltage, U16.input_voltage
  GND: U13.S, C3.0, C4.1, VCC4.-, U14.GND, U15.GND, S6.Pin_3, S6.Pin_4, U16.GND, DHT3.GND, Part5.GND
  N2: C3.1, U14.VCC, U16.output_voltage
  VDD: C4.0, U15.output_voltage, DHT3.VDD, R2.Pin_0, Part5.VCC
  N3: U14.GPIO_0, Part5.AO
  N4: U14.RST, S6.Pin_1, S6.Pin_2
  N5: U14.GPIO_2, DHT3.DATA, R2.Pin_1

custom parts:
  ESP8266 WiFi Module: Generic WiFi Module based on the ESP8266 with onboard PCB antenna and UART communications
  DHT11 Humitidy and Temperature Sensor: DHT11 Humidity and Temperature Sensor
  MQ-9 breakout: SKU: 101284
