# Fritzing sketch Programmer (saved by Fritzing 0.9.3b)

parts:
  Part4 = FTDI Basic Programmer
  U10 = ESP8266 WiFi Module [part_number=ESP8266]
  S5 = Pushbutton [package="[SMD]"]

nets:
  N1: Part4.RXI, U10.TXD
  N2: Part4.TXO, U10.RXD
  N3: Part4.POWER, U10.VCC, U10.CH_PD
  GND: Part4.GND, U10.GPIO_0, U10.GND, S5.Pin_3, S5.Pin_4
  N4: U10.RST, S5.Pin_1, S5.Pin_2

custom parts:
  ESP8266 WiFi Module: Generic WiFi Module based on the ESP8266 with onboard PCB antenna and UART communications
