# Fritzing sketch RPi (saved by Fritzing 0.9.3b)

parts:
  Raspberry_Pi_1 = Raspberry Pi 3 [part_number=RPI-3-V1.2]
  Componente2 = RFID-RC522-v2
  PIR1 = PIR sensor
  CAMERA1 = TTL Serial JPEG Camera  # not connected

nets:
  N1: Raspberry_Pi_1.GPIO2, PIR1.SIG
  3V3: Raspberry_Pi_1.3V3, Componente2.3.3V
  N2: Raspberry_Pi_1.GPIO10, Componente2.MOSI
  N3: Raspberry_Pi_1.GPIO9, Componente2.MISO
  N4: Raspberry_Pi_1.GPIO11, Componente2.SCK
  N5: Raspberry_Pi_1.GPIO8, Componente2.SDA
  N6: Raspberry_Pi_1.GPIO25, Componente2.RST
  N7: Raspberry_Pi_1.GPIO24, Componente2.GND
  GND: Raspberry_Pi_1.GND, PIR1.GND
  5V: Raspberry_Pi_1.5V, PIR1.VDD

custom parts:
  RFID-RC522-v2: A simple China made RFID-RC522 Reader; do check the pin labels, as this is a MFRC522 based clone.
  TTL Serial JPEG Camera: TTL Serial JPEG Camera with NTSC Out
